# Fritzing sketch Parallel_state_machine (saved by Fritzing 1.0.4)

parts:
  Part1 = Arduino Nano (Rev3.0)
  RED = LED - 5mm [color="Red (633nm)" current=0.030A package="5 mm [THT]"]
  YELLOW = LED - 5mm [color="Yellow (585nm)" current=0.030A package="5 mm [THT]"]
  GREEN = LED - 5mm [color="Green (565nm)" current=0.030A package="5 mm [THT]"]
  R1 = Resistor [tolerance=±5% power=0.25W resistance=220 package=THT]
  R2 = Resistor [tolerance=±5% power=0.25W resistance=220 package=THT]
  R3 = Resistor [tolerance=±5% power=0.25W resistance=220 package=THT]
  Power = Power plug

nets:
  GND: Part1.GND, R1.Pin_0, R2.Pin_0, R3.Pin_0, Power.GND
  VIN: Part1.VIN, Power.VCC
  N1: Part1.A2, GREEN.anode
  N2: Part1.A1, YELLOW.anode
  N3: Part1.A0, RED.anode
  N4: RED.cathode, R1.Pin_1
  N5: YELLOW.cathode, R2.Pin_1
  N6: GREEN.cathode, R3.Pin_1
